# Fritzing sketch fan-for-car-01 (saved by Fritzing 0.9.5d)
breadboards: 1

parts:
  LCD1 = LCD screen  # not connected
  Raspberry_Pi_1 = Raspberry Pi 3 [part_number=RPI-3-V1.2]  # not connected
  U1 = L298 [package=multiwatt15_6400bgheatsink]  # not connected
  S1 = H-Bridge with L298N
  F1 = Fan - Ventilador [package=THT]  # not connected
  F2 = Fan - Ventilador [package=THT]  # not connected
  HLK-PM1 = HLK-PM12 [part_number=HLK-PM12]

nets:
  N1: S1.12V, HLK-PM1.+Vo
  N2: S1.GND, HLK-PM1.-Vo

custom parts:
  H-Bridge with L298N: h-bridge
  Fan - Ventilador: Ventilador de 2 pines, se encuentra comunmente en computadoras de escritorio
